# Fritzing sketch coruja_gps (saved by Fritzing 1.0.7)

parts:
  Raspberry_Pi_Pico_2_W = Raspberry Pi Pico
  GPS_NEO-M8N_(GY-GPSV3) = Generic female header - metal rounded - 4 pins [package=THT]
  Leitor_microSD_(9_pinos) = Generic female header - 9 pins [package=THT]
  Display_2_4"_240x320_ST7789V_(GMT024-08-SPI8P) = Generic female header - 8 pins [package=THT]
  Encoder_KY-040 = Generic female header - metal rounded - 5 pins [package=THT]
  Entrada_12V_(pos-chave) = Generic female header - metal rounded - 3 pins [package=THT]
  F1_2_A = FUSE [package=fuse_5mm]
  TVS1_P6KE24CA_bidirecional = TVS [package=sma-diode]
  Conversor_step-down_12V->5V_(LM2596_nao_isolado) = Generic female header - metal rounded - 4 pins [package=THT]
  LED_RGB_10mm_anodo_comum = RGB LED (com. cathode, rgb) [package="5 mm [THT]"]
  R1_330R_(vermelho) = Resistor [resistance=330 package=THT]
  R2_470R_(verde) = Resistor [resistance=470 package=THT]
  R3_150R_(azul) = Resistor [resistance=150 package=THT]
  R4_1k_(base_Q1) = Resistor [resistance=1k package=THT]
  R5_1k_(GPIO0_->_GPS_RX) = Resistor [resistance=1k package=THT]
  Q1_BC337_(nao_BC547) = TRANSISTOR_NPN [package=to-92]
  D1_Schottky_1N5817/1N5819 = Schottky Diode [package="300 mil [THT]"]
  C1_470uF_25V_105C = Electrolytic Capacitor [capacitance=470µF package="200 mil [THT, electrolytic]"]
  C5_470uF_50V_105C_(entrada_12V) = Electrolytic Capacitor [capacitance=470µF package="200 mil [THT, electrolytic]"]
  C2_100nF_(filtro_VSYS) = Ceramic Capacitor [capacitance=100nF package="100 mil [THT, multilayer]"]
  BZ1_SFM-27_(fios_diretos) = Piezo Speaker

nets:
  N1: Raspberry_Pi_Pico_2_W.pin_1, R5_1k_(GPIO0_->_GPS_RX).Pin_0
  N2: Raspberry_Pi_Pico_2_W.pin_2, GPS_NEO-M8N_(GY-GPSV3).pin3
  N3: Raspberry_Pi_Pico_2_W.pin_3, Raspberry_Pi_Pico_2_W.pin_38, GPS_NEO-M8N_(GY-GPSV3).pin4, Leitor_microSD_(9_pinos).pin2, Display_2_4"_240x320_ST7789V_(GMT024-08-SPI8P).pin1, Encoder_KY-040.pin1, Entrada_12V_(pos-chave).pin3, TVS1_P6KE24CA_bidirecional.2, Conversor_step-down_12V->5V_(LM2596_nao_isolado).pin2, Conversor_step-down_12V->5V_(LM2596_nao_isolado).pin4, Q1_BC337_(nao_BC547).E, C1_470uF_25V_105C.-, C5_470uF_50V_105C_(entrada_12V).-, C2_100nF_(filtro_VSYS).1
  N4: Raspberry_Pi_Pico_2_W.pin_4, Encoder_KY-040.pin5
  N5: Raspberry_Pi_Pico_2_W.pin_5, Encoder_KY-040.pin4
  N6: Raspberry_Pi_Pico_2_W.pin_6, Encoder_KY-040.pin3
  N7: Raspberry_Pi_Pico_2_W.pin_7, R4_1k_(base_Q1).Pin_0
  N8: Raspberry_Pi_Pico_2_W.pin_9, R3_150R_(azul).Pin_0
  N9: Raspberry_Pi_Pico_2_W.pin_10, R2_470R_(verde).Pin_0
  N10: Raspberry_Pi_Pico_2_W.pin_11, R1_330R_(vermelho).Pin_0
  N11: Raspberry_Pi_Pico_2_W.pin_14, Display_2_4"_240x320_ST7789V_(GMT024-08-SPI8P).pin3
  N12: Raspberry_Pi_Pico_2_W.pin_15, Display_2_4"_240x320_ST7789V_(GMT024-08-SPI8P).pin4
  N13: Raspberry_Pi_Pico_2_W.pin_16, Display_2_4"_240x320_ST7789V_(GMT024-08-SPI8P).pin7
  N14: Raspberry_Pi_Pico_2_W.pin_17, Display_2_4"_240x320_ST7789V_(GMT024-08-SPI8P).pin6
  N15: Raspberry_Pi_Pico_2_W.pin_19, Display_2_4"_240x320_ST7789V_(GMT024-08-SPI8P).pin5
  N16: Raspberry_Pi_Pico_2_W.pin_20, Display_2_4"_240x320_ST7789V_(GMT024-08-SPI8P).pin8
  N17: Raspberry_Pi_Pico_2_W.pin_21, Leitor_microSD_(9_pinos).pin4
  N18: Raspberry_Pi_Pico_2_W.pin_22, Leitor_microSD_(9_pinos).pin6
  N19: Raspberry_Pi_Pico_2_W.pin_24, Leitor_microSD_(9_pinos).pin3
  N20: Raspberry_Pi_Pico_2_W.pin_25, Leitor_microSD_(9_pinos).pin5
  N21: Raspberry_Pi_Pico_2_W.pin_36, Leitor_microSD_(9_pinos).pin1, Encoder_KY-040.pin2, LED_RGB_10mm_anodo_comum.common_cathode
  N22: Raspberry_Pi_Pico_2_W.pin_39, GPS_NEO-M8N_(GY-GPSV3).pin1, Display_2_4"_240x320_ST7789V_(GMT024-08-SPI8P).pin2, D1_Schottky_1N5817/1N5819.cathode, C1_470uF_25V_105C.+, C2_100nF_(filtro_VSYS).0
  N23: GPS_NEO-M8N_(GY-GPSV3).pin2, R5_1k_(GPIO0_->_GPS_RX).Pin_1
  N24: Entrada_12V_(pos-chave).pin1, F1_2_A.1
  N25: F1_2_A.2, TVS1_P6KE24CA_bidirecional.1, Conversor_step-down_12V->5V_(LM2596_nao_isolado).pin1, C5_470uF_50V_105C_(entrada_12V).+, BZ1_SFM-27_(fios_diretos).pin1
  N26: Conversor_step-down_12V->5V_(LM2596_nao_isolado).pin3, D1_Schottky_1N5817/1N5819.anode
  N27: LED_RGB_10mm_anodo_comum.red_anode, R1_330R_(vermelho).Pin_1
  N28: LED_RGB_10mm_anodo_comum.green_anode, R2_470R_(verde).Pin_1
  N29: LED_RGB_10mm_anodo_comum.blue_anode, R3_150R_(azul).Pin_1
  N30: R4_1k_(base_Q1).Pin_1, Q1_BC337_(nao_BC547).B
  N31: Q1_BC337_(nao_BC547).C, BZ1_SFM-27_(fios_diretos).pin2

custom parts:
  Raspberry Pi Pico: Raspberry Pi Pico. Based around the RP2040 microcontroller the Pico is a low cost microcontroller device bringing Raspberry Pi quality, cost, and easy of use to the microcontroller space. Jan 2021, Split part in to two versions: tht (this one) and SMD. This one will drill holes for a .1 in header in pcb to allow plugging in the module as well as providing pads to solder the module to the top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
